# Fritzing sketch circuit (saved by Fritzing 0.9.7b)

parts:
  Mod1 = Raspberry Pi 4B
  U1 = Vibration Motor- ROB-08449 [package=vibe-motor-10mm]
  U2 = TRANSCHIPTC5747 [package=camera_sfv24r-2st_2]  # not connected
  J1 = Piezo Speaker

nets:
  N1: Mod1.GND, U1.+, J1.pin1
  N2: Mod1.GPIO14, U1.-
  N3: Mod1.GPIO15, J1.pin2

notes:
  Pi Camera
  Raspberry Pi 4
  Vibration Motor
  Buzzer
